// Logisim project PROCESSEUR_REGISTRE.circ as structural Verilog
module simpleBitAdder (
  input  in_1,
  input  in_2,
  input  in_3,
  output out_4,
  output out_5
);

  wire and_1_out, and_2_out, xor_1_out;

  xor xor_1 (xor_1_out, in_1, in_2);
  and and_1 (and_1_out, in_1, in_2);
  and and_2 (and_2_out, xor_1_out, in_3);
  xor xor_2 (out_4, in_3, xor_1_out);
  xor xor_3 (out_5, and_2_out, and_1_out);
endmodule

module Add (
  input  [7:0] in_1,
  input  [7:0] in_2,
  output [7:0] out_3,
  output out_4
);

  wire and_1_out, simplebitadder_1_out_5, simplebitadder_2_out_5, simplebitadder_3_out_5,
       simplebitadder_4_out_5, simplebitadder_5_out_5, simplebitadder_6_out_5;

  xor xor_1 (out_3[0], in_1[0], in_2[0]);
  and and_1 (and_1_out, in_1[0], in_2[0]);
  simpleBitAdder simplebitadder_1 (
    .in_1(and_1_out), .in_2(in_1[1]), .in_3(in_2[1]), .out_4(out_3[1]), .out_5(simplebitadder_1_out_5));
  simpleBitAdder simplebitadder_2 (
    .in_1(simplebitadder_1_out_5), .in_2(in_1[2]), .in_3(in_2[2]), .out_4(out_3[2]),
    .out_5(simplebitadder_2_out_5));
  simpleBitAdder simplebitadder_3 (
    .in_1(simplebitadder_2_out_5), .in_2(in_1[3]), .in_3(in_2[3]), .out_4(out_3[3]),
    .out_5(simplebitadder_3_out_5));
  simpleBitAdder simplebitadder_4 (
    .in_1(simplebitadder_3_out_5), .in_2(in_1[4]), .in_3(in_2[4]), .out_4(out_3[4]),
    .out_5(simplebitadder_4_out_5));
  simpleBitAdder simplebitadder_5 (
    .in_1(simplebitadder_4_out_5), .in_2(in_1[5]), .in_3(in_2[5]), .out_4(out_3[5]),
    .out_5(simplebitadder_5_out_5));
  simpleBitAdder simplebitadder_6 (
    .in_1(simplebitadder_5_out_5), .in_2(in_1[6]), .in_3(in_2[6]), .out_4(out_3[6]),
    .out_5(simplebitadder_6_out_5));
  simpleBitAdder simplebitadder_7 (
    .in_1(simplebitadder_6_out_5), .in_2(in_1[7]), .in_3(in_2[7]), .out_4(out_3[7]), .out_5(out_4));
endmodule

module Sub (
  input  [7:0] in_1,
  input  [7:0] in_2,
  output [7:0] out_3,
  output out_4
);

  wire not_1_out, not_2_out, not_3_out, not_4_out, not_5_out, not_6_out, not_7_out, not_8_out,
       simplebitadder_1_out_5, simplebitadder_2_out_5, simplebitadder_3_out_5, simplebitadder_4_out_5,
       simplebitadder_5_out_5, simplebitadder_6_out_5, simplebitadder_7_out_5, xor_1_out, xor_2_out;

  not not_1 (not_1_out, in_2[0]);
  not not_2 (not_2_out, in_2[1]);
  not not_3 (not_3_out, in_2[2]);
  not not_4 (not_4_out, in_2[3]);
  not not_5 (not_5_out, in_2[4]);
  not not_6 (not_6_out, in_2[5]);
  not not_7 (not_7_out, in_2[6]);
  not not_8 (not_8_out, in_2[7]);
  simpleBitAdder simplebitadder_1 (
    .in_1(in_1[0]), .in_2(not_1_out), .in_3(1'b1), .out_4(out_3[0]), .out_5(simplebitadder_1_out_5));
  simpleBitAdder simplebitadder_2 (
    .in_1(simplebitadder_1_out_5), .in_2(in_1[1]), .in_3(not_2_out), .out_4(out_3[1]),
    .out_5(simplebitadder_2_out_5));
  simpleBitAdder simplebitadder_3 (
    .in_1(simplebitadder_2_out_5), .in_2(in_1[2]), .in_3(not_3_out), .out_4(out_3[2]),
    .out_5(simplebitadder_3_out_5));
  simpleBitAdder simplebitadder_4 (
    .in_1(simplebitadder_3_out_5), .in_2(in_1[3]), .in_3(not_4_out), .out_4(out_3[3]),
    .out_5(simplebitadder_4_out_5));
  simpleBitAdder simplebitadder_5 (
    .in_1(simplebitadder_4_out_5), .in_2(in_1[4]), .in_3(not_5_out), .out_4(out_3[4]),
    .out_5(simplebitadder_5_out_5));
  simpleBitAdder simplebitadder_6 (
    .in_1(simplebitadder_5_out_5), .in_2(in_1[5]), .in_3(not_6_out), .out_4(out_3[5]),
    .out_5(simplebitadder_6_out_5));
  simpleBitAdder simplebitadder_7 (
    .in_1(simplebitadder_6_out_5), .in_2(in_1[6]), .in_3(not_7_out), .out_4(out_3[6]),
    .out_5(simplebitadder_7_out_5));
  simpleBitAdder simplebitadder_8 (
    .in_1(simplebitadder_7_out_5), .in_2(in_1[7]), .in_3(not_8_out), .out_4(out_3[7]));  // open: out_5
  xor xor_1 (xor_1_out, in_1[7], in_2[7]);
  xor xor_2 (xor_2_out, in_1[7], out_3[7]);
  and and_1 (out_4, xor_1_out, xor_2_out);
endmodule

module And8Bit (
  input  [7:0] in_1,
  input  [7:0] in_2,
  output [7:0] out_3
);

  assign out_3 = in_1 & in_2;  // AND_Gate and_1, 8 bits wide
endmodule

module Or8Bit (
  input  [7:0] in_1,
  input  [7:0] in_2,
  output [7:0] out_3
);

  assign out_3 = in_1 | in_2;  // OR_Gate or_1, 8 bits wide
endmodule

module Xor8Bit (
  input  [7:0] in_1,
  input  [7:0] in_2,
  output [7:0] out_3
);

  assign out_3 = in_1 ^ in_2;  // XOR_Gate xor_1, 8 bits wide
endmodule

module Egal (
  input  [7:0] in_1,
  input  [7:0] in_2,
  output [7:0] out_3
);

  wire [7:0] not_1_out, xor8bit_1_out_3;

  assign not_1_out = ~in_2;  // NOT_Gate not_1, 8 bits wide
  Xor8Bit xor8bit_1 (.in_1(in_1), .in_2(not_1_out), .out_3(xor8bit_1_out_3));
  and and_1 (out_3[0], xor8bit_1_out_3[0], xor8bit_1_out_3[1], xor8bit_1_out_3[2], xor8bit_1_out_3[3], xor8bit_1_out_3[4], xor8bit_1_out_3[5], xor8bit_1_out_3[6], xor8bit_1_out_3[7]);

  assign out_3[7:1] = {7{1'b0}};
endmodule

module Sup (
  input  [7:0] in_1,
  input  [7:0] in_2,
  output [7:0] out_3
);

  wire or_1_out;
  wire [7:0] egal_1_out_3, sub_1_out_3;

  Sub sub_1 (.in_1(in_1), .in_2(in_2), .out_3(sub_1_out_3));  // open: out_4
  Egal egal_1 (.in_1(in_1), .in_2(in_2), .out_3(egal_1_out_3));
  or or_1 (or_1_out, sub_1_out_3[7], egal_1_out_3[0]);
  not not_1 (out_3[0], or_1_out);

  assign out_3[7:1] = {7{1'b0}};
endmodule

module Inf (
  input  [7:0] in_1,
  input  [7:0] in_2,
  output [7:0] out_3
);

  wire [7:0] sub_1_out_3;

  Sub sub_1 (.in_1(in_1), .in_2(in_2), .out_3(sub_1_out_3));  // open: out_4
  not not_1 (out_3[7], sub_1_out_3[7]);

  assign out_3[6:0] = {7{1'b0}};
endmodule

module Diff (
  input  [7:0] in_1,
  input  [7:0] in_2,
  output [7:0] out_3
);

  wire [0:0] egal_1_out_3;

  Egal egal_1 (.in_1(in_1), .in_2(in_2), .out_3({out_3[7:1], egal_1_out_3[0]}));
  not not_1 (out_3[0], egal_1_out_3[0]);
endmodule

module ALU (
  input  [7:0] A,
  input  [7:0] B,
  input  [7:0] Sortie,
  input  [3:0] Selecteur,
  output Erreur
);

  wire multiplex_operation_1_out_5;
  wire [7:0] multiplex_comparaison_1_out_4, multiplex_logique_1_out_4, multiplex_operation_1_out_4;

  Multiplex_Operation multiplex_operation_1 (
    .in_1(A), .in_2(B), .in_3(Selecteur[1:0]), .out_4(multiplex_operation_1_out_4),
    .out_5(multiplex_operation_1_out_5));
  Multiplex_Comparaison multiplex_comparaison_1 (
    .in_1(A), .in_2(B), .in_3(Selecteur[1:0]), .out_4(multiplex_comparaison_1_out_4));
  Multiplex_Logique multiplex_logique_1 (.in_1(A), .in_2(B), .in_3(Selecteur[1:0]), .out_4(multiplex_logique_1_out_4));
  Multiplexer #(.select(2), .width(8)) multiplexer_1 (
    .in0(multiplex_operation_1_out_4), .in1(multiplex_comparaison_1_out_4), .in2(multiplex_logique_1_out_4),
    .out(Sortie), .sel(Selecteur[3:2]));  // open: in3
  Multiplexer #(.select(2)) multiplexer_2 (
    .in0(multiplex_operation_1_out_5), .out(Erreur), .sel(Selecteur[3:2]));  // open: in1, in2, in3
endmodule

module Multiplex_Operation (
  input  [7:0] in_1,
  input  [7:0] in_2,
  input  [1:0] in_3,
  output [7:0] out_4,
  output out_5
);

  wire add_1_out_4, sub_1_out_4;
  wire [7:0] add_1_out_3, sub_1_out_3;

  Add add_1 (.in_1(in_1), .in_2(in_2), .out_3(add_1_out_3), .out_4(add_1_out_4));
  Sub sub_1 (.in_1(in_1), .in_2(in_2), .out_3(sub_1_out_3), .out_4(sub_1_out_4));
  Multiplexer #(.select(2)) multiplexer_1 (
    .in0(add_1_out_4), .in1(sub_1_out_4), .out(out_5), .sel(in_3));  // open: in2, in3
  Multiplexer #(.select(2), .width(8)) multiplexer_2 (
    .in0(add_1_out_3), .in1(sub_1_out_3), .out(out_4), .sel(in_3));  // open: in2, in3
endmodule

module Multiplex_Comparaison (
  input  [7:0] in_1,
  input  [7:0] in_2,
  input  [1:0] in_3,
  output [7:0] out_4
);

  wire [7:0] egal_1_out_3, inf_1_out_3, sup_1_out_3;

  Egal egal_1 (.in_1(in_1), .in_2(in_2), .out_3(egal_1_out_3));
  Sup sup_1 (.in_1(in_1), .in_2(in_2), .out_3(sup_1_out_3));
  Inf inf_1 (.in_1(in_1), .in_2(in_2), .out_3(inf_1_out_3));
  Multiplexer #(.select(2), .width(8)) multiplexer_1 (
    .in0(egal_1_out_3), .in1(sup_1_out_3), .in2(inf_1_out_3), .in3(inf_1_out_3), .out(out_4), .sel(in_3));
endmodule

module Multiplex_Logique (
  input  [7:0] in_1,
  input  [7:0] in_2,
  input  [1:0] in_3,
  output [7:0] out_4
);

  wire [7:0] and8bit_1_out_3, or8bit_1_out_3, xor8bit_1_out_3;

  And8Bit and8bit_1 (.in_1(in_1), .in_2(in_2), .out_3(and8bit_1_out_3));
  Or8Bit or8bit_1 (.in_1(in_1), .in_2(in_2), .out_3(or8bit_1_out_3));
  Xor8Bit xor8bit_1 (.in_1(in_1), .in_2(in_2), .out_3(xor8bit_1_out_3));
  Multiplexer #(.select(2), .width(8)) multiplexer_1 (
    .in0(and8bit_1_out_3), .in1(or8bit_1_out_3), .in2(xor8bit_1_out_3), .out(out_4), .sel(in_3));  // open: in3
endmodule

module Registre (
  input  [7:0] in_1,
  output [7:0] out_2
);

  wire clock_1_out;

  Clock #(.highDuration(20), .lowDuration(20)) clock_1 (.out(clock_1_out));
  D_Flip_Flop d_ff_1 (.D(in_1[0]), .clk(clock_1_out), .Q(out_2[0]));  // open: Qn, preset, reset
  D_Flip_Flop d_ff_2 (.D(in_1[1]), .clk(clock_1_out), .Q(out_2[1]));  // open: Qn, preset, reset
  D_Flip_Flop d_ff_3 (.D(in_1[2]), .clk(clock_1_out), .Q(out_2[2]));  // open: Qn, preset, reset
  D_Flip_Flop d_ff_4 (.D(in_1[3]), .clk(clock_1_out), .Q(out_2[3]));  // open: Qn, preset, reset
  D_Flip_Flop d_ff_5 (.D(in_1[4]), .clk(clock_1_out), .Q(out_2[4]));  // open: Qn, preset, reset
  D_Flip_Flop d_ff_6 (.D(in_1[5]), .clk(clock_1_out), .Q(out_2[5]));  // open: Qn, preset, reset
  D_Flip_Flop d_ff_7 (.D(in_1[6]), .clk(clock_1_out), .Q(out_2[6]));  // open: Qn, preset, reset
  D_Flip_Flop d_ff_8 (.D(in_1[7]), .clk(clock_1_out), .Q(out_2[7]));  // open: Qn, preset, reset
endmodule

module Registre_WE (
  input  in_1
);

  wire [7:0] multiplexer_1_out, registre_1_out_2;

  Multiplexer #(.width(8)) multiplexer_1 (
    .in0(registre_1_out_2), .in1(multiplexer_1_out), .out(multiplexer_1_out), .sel(in_1));
  Registre registre_1 (.in_1(multiplexer_1_out), .out_2(registre_1_out_2));
endmodule
